// Logisim project InitialCircuit.circ as structural Verilog: 1 circuit, main circuit main
// X=!(A+B)!(!C+!D)!(!A+B)
module main (
  input  A,
  input  B,
  input  C,
  input  X,
  input  D
);

  wire and_1_out, not_1_out, not_2_out, not_3_out, not_4_out, or_1_out, or_2_out, or_3_out;

  not not_1 (not_1_out, C);
  not not_2 (not_2_out, D);
  not not_3 (not_3_out, A);
  or or_1 (or_1_out, A, B);
  or or_2 (or_2_out, not_1_out, not_2_out);
  or or_3 (or_3_out, B, not_3_out);
  not not_4 (not_4_out, and_1_out);
  and and_1 (and_1_out, or_1_out, or_2_out, or_3_out);

  // Notes on the sheet:
  //   X=!(A+B)!(!C+!D)!(!A+B)
endmodule
