// Logisim project Lab Assignment 1.circ as structural Verilog: 1 circuit, main circuit main
module main (
  input  A,
  input  B
);

  wire A_B_2_out, A_B_3_out, A_B_out, not_1_out, not_2_out;

  not not_1 (not_1_out, B);
  not not_2 (not_2_out, A);
  and A_B (A_B_out, A, not_1_out);
  nor A_B_2 (A_B_2_out, not_1_out, not_2_out);
  and A_B_3 (A_B_3_out, B, not_2_out);
  LED led_1 (.in(A_B_out));
  LED led_2 (.in(A_B_2_out));
  LED led_3 (.in(A_B_3_out));
endmodule
