// Logisim project testclock.circ as structural Verilog: 1 circuit, main circuit main
module main (
  input  in_1
);

  wire bcd_to_7_segment_decoder_3_p1, binary_to_bcd_converter_1_p2, binary_to_bcd_converter_1_p4, clock,
       comparator_1_eq;
  wire [7:0] counter_1_q;

  Clock clock_1 (.out(clock));
  Counter #(.max('hf)) counter_1 (.clr(in_1), .clk(clock), .Q(counter_1_q));  // open: load, up, count, D, carry
  _7_Segment_Display u_7_segment_display_1 ();  // open: g, f, a, b, e, d, c, dp
  // BCD_to_7_Segment_decoder bcd_to_7_segment_decoder_1: pin names not known
  // Binary_to_BCD_converter #(.binvalue(8)) binary_to_bcd_converter_1: pin names not known; wires that end beside it: counter_1_q, binary_to_bcd_converter_1_p2, binary_to_bcd_converter_1_p2, binary_to_bcd_converter_1_p4
  _7_Segment_Display u_7_segment_display_2 ();  // open: g, f, a, b, e, d, c, dp
  _7_Segment_Display u_7_segment_display_3 ();  // open: g, f, a, b, e, d, c, dp
  // BCD_to_7_Segment_decoder bcd_to_7_segment_decoder_2: pin names not known; wires that end beside it: binary_to_bcd_converter_1_p4
  // BCD_to_7_Segment_decoder bcd_to_7_segment_decoder_3: pin names not known; wires that end beside it: bcd_to_7_segment_decoder_3_p1, bcd_to_7_segment_decoder_3_p1
  Comparator comparator_1 (.a(8'hf), .b(counter_1_q), .eq(comparator_1_eq));  // open: gt, lt
  LED led_1 (.in(comparator_1_eq));
  // Digital_Oscilloscope digital_oscilloscope_1: pin names not known; wires that end beside it: clock, comparator_1_eq
endmodule
